# Fritzing sketch PlayTunes (saved by Fritzing 0.9.3b)

parts:
  Part1 = Arduino Uno (Rev3) - ICSP
  S1 = Momentary Switch [package=ksa_sealed_tac_switch]
  S2 = Momentary Switch [package=ksa_sealed_tac_switch]
  Part2 = LCD1602-I2C
  J1 = Piezo Speaker
  J2 = Piezo Speaker

nets:
  N1: Part1.A4/SDA, Part2.SDA
  N2: Part1.A5/SCL, Part2.SCL
  N3: Part1.D12/MISO, J2.pin2
  N4: Part1.D13/SCK, J1.pin2
  GND: Part1.GND, Part2.GND, J1.pin1, J2.pin1
  N5: Part1.D2, S1.4
  N6: Part1.D3_PWM, S2.4
  5V: Part1.5V, Part2.VCC
  N7: Part1.VIN, S1.2

custom parts:
  LCD1602-I2C: A standard character display, usually with 2x16 characters. Comes in many colors with LCM1602 IIC attached.
